// Logisim project syndrome_calc.circ as structural Verilog: 1 circuit, main circuit main
module main (
);

  wire dipswitch_1_p1, dipswitch_1_p2, dipswitch_1_p3, dipswitch_1_p4, dipswitch_1_p5, dipswitch_1_p6,
       dipswitch_1_p7, nand_1_out, nand_2_out, nand_3_out, nand_4_out, nand_5_out, nand_6_out, nand_7_out,
       not_1_out, not_2_out, not_3_out, not_4_out, not_5_out, not_6_out, not_7_out, not_8_out, not_9_out,
       not_10_out, not_11_out, not_12_out, not_13_out, not_14_out, not_15_out, not_16_out, xor_1_out,
       xor_2_out, xor_3_out, xor_4_out, xor_5_out, xor_6_out, xor_7_out, xor_8_out, xor_9_out, xor_10_out,
       xor_11_out, xor_12_out, xor_13_out, xor_14_out, xor_15_out, xor_16_out;

  // DipSwitch #(.number(7)) dipswitch_1: pin names not known; wires that end beside it: dipswitch_1_p1, dipswitch_1_p2, dipswitch_1_p3, dipswitch_1_p4, dipswitch_1_p5, dipswitch_1_p6, dipswitch_1_p7
  xor xor_1 (xor_1_out, dipswitch_1_p5, dipswitch_1_p7);
  xor xor_2 (xor_2_out, dipswitch_1_p6, dipswitch_1_p7);
  xor xor_3 (xor_3_out, dipswitch_1_p5, dipswitch_1_p7);
  xor xor_4 (xor_4_out, dipswitch_1_p1, xor_5_out);
  xor xor_5 (xor_5_out, dipswitch_1_p3, xor_1_out);
  xor xor_6 (xor_6_out, dipswitch_1_p2, xor_7_out);
  xor xor_7 (xor_7_out, dipswitch_1_p3, xor_2_out);
  xor xor_8 (xor_8_out, dipswitch_1_p4, xor_9_out);
  xor xor_9 (xor_9_out, dipswitch_1_p6, xor_3_out);
  not not_1 (not_1_out, xor_6_out);
  not not_2 (not_2_out, xor_8_out);
  not not_3 (not_3_out, xor_4_out);
  not not_4 (not_4_out, xor_8_out);
  not not_5 (not_5_out, xor_8_out);
  not not_6 (not_6_out, xor_4_out);
  not not_7 (not_7_out, xor_6_out);
  not not_8 (not_8_out, xor_6_out);
  not not_9 (not_9_out, xor_4_out);
  nand nand_1 (nand_1_out, xor_4_out, not_1_out, not_2_out);
  nand nand_2 (nand_2_out, not_3_out, xor_6_out, not_4_out);
  nand nand_3 (nand_3_out, xor_4_out, xor_6_out, not_5_out);
  nand nand_4 (nand_4_out, not_6_out, not_7_out, xor_8_out);
  nand nand_5 (nand_5_out, xor_4_out, not_8_out, xor_8_out);
  nand nand_6 (nand_6_out, not_9_out, xor_6_out, xor_8_out);
  nand nand_7 (nand_7_out, xor_4_out, xor_6_out, xor_8_out);
  xor xor_10 (xor_10_out, dipswitch_1_p1, nand_1_out);
  not not_10 (not_10_out, xor_10_out);
  xor xor_11 (xor_11_out, dipswitch_1_p2, nand_2_out);
  not not_11 (not_11_out, xor_11_out);
  xor xor_12 (xor_12_out, dipswitch_1_p3, nand_3_out);
  not not_12 (not_12_out, xor_12_out);
  xor xor_13 (xor_13_out, dipswitch_1_p4, nand_4_out);
  not not_13 (not_13_out, xor_13_out);
  xor xor_14 (xor_14_out, dipswitch_1_p5, nand_5_out);
  not not_14 (not_14_out, xor_14_out);
  xor xor_15 (xor_15_out, dipswitch_1_p6, nand_6_out);
  not not_15 (not_15_out, xor_15_out);
  xor xor_16 (xor_16_out, dipswitch_1_p7, nand_7_out);
  not not_16 (not_16_out, xor_16_out);
  LED led_1 (.in(not_16_out));
  LED led_2 (.in(not_15_out));
  LED led_3 (.in(not_14_out));
  LED led_4 (.in(not_13_out));
  LED led_5 (.in(not_12_out));
  LED led_6 (.in(not_11_out));
  LED led_7 (.in(not_10_out));
endmodule
